# Fritzing sketch ejercicio_2_esquema (saved by Fritzing 0.9.3b)
breadboards: 1

parts:
  WeMos_D1_Mini1 = WeMos D1 Mini
  PIR1 = PIR sensor

nets:
  3V3: WeMos_D1_Mini1.3V3, PIR1.VDD
  N1: WeMos_D1_Mini1.D3, PIR1.SIG
  N2: WeMos_D1_Mini1.G, PIR1.GND
